// Logisim project RISC 32 BIT DECODE.circ as structural Verilog: 1 circuit, main circuit main
module main (
  input  [31:0] Instruction,
  output out_2,
  output out_3,
  output out_4,
  output out_5,
  output out_6,
  output out_7,
  output out_8,
  output out_9,
  output out_10,
  output out_11,
  output out_12,
  output out_13,
  output out_14,
  output out_15,
  output out_16,
  output out_17,
  output out_18,
  output out_19,
  output out_20,
  output out_21,
  output out_22,
  output out_23,
  output Arithmetic,
  output Logic,
  output BranchJump,
  output RegInstr,
  output Stack,
  output out_29,
  output out_30,
  output out_31,
  output out_32,
  output out_33,
  output out_34,
  output [7:0] out_35,
  output [7:0] out_36,
  output [7:0] out_37,
  output [1:0] out_38
);

  and and_1 (Arithmetic, ~Instruction[31], ~Instruction[30], Instruction[29]);  // AND_Gate
  and and_2 (Logic, ~Instruction[31], ~Instruction[30], ~Instruction[29]);  // AND_Gate
  and and_3 (BranchJump, ~Instruction[31], Instruction[30]);  // AND_Gate
  and and_4 (RegInstr, Instruction[31], Instruction[30], ~Instruction[29]);  // AND_Gate
  and and_5 (Stack, ~Instruction[31], Instruction[30], Instruction[29]);  // AND_Gate
  Decoder #(.select(3)) decoder_1 (
    .out1(out_9), .out2(out_10), .out3(out_11), .out4(out_12), .out5(out_13), .out6(out_14),
    .sel(Instruction[28:26]), .en(Logic));  // open: out0, out7
  Decoder decoder_2 (.out0(out_15), .out1(out_16), .sel(Instruction[26]), .en(Stack));
  Decoder #(.select(3)) decoder_3 (
    .out0(out_17), .out1(out_18), .out2(out_19), .out3(out_20), .out4(out_21), .out5(out_22), .out6(out_23),
    .out7(out_29), .sel(Instruction[28:26]), .en(BranchJump));
  Decoder #(.select(3)) decoder_4 (
    .out0(out_31), .out1(out_32), .out2(out_33), .out3(out_34), .sel(Instruction[28:26]), .en(RegInstr));  // open: out4, out5, out6, out7
  Decoder #(.select(3)) decoder_5 (
    .out0(out_2), .out1(out_3), .out2(out_4), .out3(out_5), .out4(out_6), .out5(out_7), .out6(out_8),
    .sel(Instruction[28:26]), .en(Arithmetic));  // open: out7
  and and_6 (out_30, BranchJump, Instruction[29], ~Instruction[26], ~Instruction[27], ~Instruction[28]);  // AND_Gate

  assign out_35 = Instruction[23:16];
  assign out_36 = Instruction[15:8];
  assign out_37 = Instruction[7:0];
  assign out_38 = Instruction[25:24];

  // Other names for the same wires on the sheet: ADD = out_2; AND = out_9; BEQ = out_19; BGE = out_21; BGT = out_20;
  //   BLEQ = out_22; BLSS = out_18; BNEQ = out_23; CLR = out_34; CMP = out_12; DEC = out_8; DIV = out_5; INC = out_7;
  //   First[7:0] = Instruction[7:0]; OP2[7:0] = Instruction[7:0]; OP1[7:0] = Instruction[15:8];
  //   Second[7:0] = Instruction[15:8]; Dest[7:0] = Instruction[23:16]; Third[7:0] = Instruction[23:16];
  //   Fourth[7:0] = Instruction[31:24]; Number[1:0] = Instruction[25:24]; Instruction_t[2:0] = Instruction[28:26];
  //   IR29 = Instruction[29]; Type[2:0] = Instruction[31:29]; IR30 = Instruction[30]; IR31 = Instruction[31];
  //   JSR = out_29; JUMP = out_17; LD = out_31; LSH = out_13; MOD = out_6; MOV = out_33; MUL = out_4; OR = out_10;
  //   POP = out_15; PUSH = out_16; RSH = out_14; RTS = out_30; ST = out_32; SUB = out_3; XOR = out_11
endmodule
