// Logisim project RISC 32 BIT REGISTERS.circ as structural Verilog: 1 circuit, main circuit main
module main (
);

  wire Clock, Clr0, Clr1, Clr2, Clr3, Clr4, Clr5, Clr6, Clr7, Clr8, Clr9, Clr10, Clr11, Clr12, Clr13, Clr14,
       Clr15, Clr16, Clr17, Clr18, Clr19, Clr20, Clr21, Clr22, Clr23, Clr24, Clr25, Clr26, Clr27, Clr28,
       Clr29, Clr30, Clr31, En0, En1, En2, En3, En4, En5, En6, En7, En8, En9, En10, En11, En12, En13, En14,
       En15, En16, En17, En18, En19, En20, En21, En22, En23, En24, En25, En26, En27, En28, En29, En30, En31,
       EnCLR, EnRC;
  wire [4:0] CLR, SelectRC;
  wire [31:0] Input, Out14, OutR0, OutR1, OutR2, OutR3, OutR4, OutR5, OutR6, OutR7, OutR8, OutR9, OutR10,
       OutR11, OutR12, OutR13, OutR15, OutR16, OutR17, OutR18, OutR19, OutR20, OutR21, OutR22, OutR23,
       OutR24, OutR25, OutR26, OutR27, OutR28, OutR29, OutR30, OutR31;

  Clock clock_1 (.out(Clock));
  Demultiplexer #(.select(5)) demultiplexer_1 (
    .out0(En0), .out1(En1), .out2(En2), .out3(En3), .out4(En4), .out5(En5), .out6(En6), .out7(En7),
    .out8(En8), .out9(En9), .out10(En10), .out11(En11), .out12(En12), .out13(En13), .out14(En14),
    .out15(En15), .out16(En16), .out17(En17), .out18(En18), .out19(En19), .out20(En20), .out21(En21),
    .out22(En22), .out23(En23), .out24(En24), .out25(En25), .out26(En26), .out27(En27), .out28(En28),
    .out29(En29), .out30(En30), .out31(En31), .in(1'b1), .sel(SelectRC), .en(EnRC));
  Register #(.width(32)) R0 (.D(Input), .en(En0), .Q(OutR0), .clk(Clock), .clr(Clr0));
  Register #(.width(32)) R8 (.D(Input), .en(En8), .Q(OutR8), .clk(Clock), .clr(Clr8));
  Register #(.width(32)) R16 (.D(Input), .en(En16), .Q(OutR16), .clk(Clock), .clr(Clr16));
  Register #(.width(32)) R24 (.D(Input), .en(En24), .Q(OutR24), .clk(Clock), .clr(Clr24));
  Register #(.width(32)) R17 (.D(Input), .en(En17), .Q(OutR17), .clk(Clock), .clr(Clr17));
  Register #(.width(32)) R25 (.D(Input), .en(En25), .Q(OutR25), .clk(Clock), .clr(Clr25));
  Register #(.width(32)) R1 (.D(Input), .en(En1), .Q(OutR1), .clk(Clock), .clr(Clr1));
  Register #(.width(32)) R9 (.D(Input), .en(En9), .Q(OutR9), .clk(Clock), .clr(Clr9));
  Register #(.width(32)) R2 (.D(Input), .en(En2), .Q(OutR2), .clk(Clock), .clr(Clr2));
  Register #(.width(32)) R10 (.D(Input), .en(En10), .Q(OutR10), .clk(Clock), .clr(Clr10));
  Register #(.width(32)) R18 (.D(Input), .en(En18), .Q(OutR18), .clk(Clock), .clr(Clr18));
  Register #(.width(32)) R26 (.D(Input), .en(En26), .Q(OutR26), .clk(Clock), .clr(Clr26));
  Demultiplexer #(.select(5)) demultiplexer_2 (
    .out0(Clr0), .out1(Clr1), .out2(Clr2), .out3(Clr3), .out4(Clr4), .out5(Clr5), .out6(Clr6), .out7(Clr7),
    .out8(Clr8), .out9(Clr9), .out10(Clr10), .out11(Clr11), .out12(Clr12), .out13(Clr13), .out14(Clr14),
    .out15(Clr15), .out16(Clr16), .out17(Clr17), .out18(Clr18), .out19(Clr19), .out20(Clr20), .out21(Clr21),
    .out22(Clr22), .out23(Clr23), .out24(Clr24), .out25(Clr25), .out26(Clr26), .out27(Clr27), .out28(Clr28),
    .out29(Clr29), .out30(Clr30), .out31(Clr31), .in(1'b1), .sel(CLR), .en(EnCLR));
  Register #(.width(32)) R3 (.D(Input), .en(En3), .Q(OutR3), .clk(Clock), .clr(Clr3));
  Register #(.width(32)) R11 (.D(Input), .en(En11), .Q(OutR11), .clk(Clock), .clr(Clr11));
  Register #(.width(32)) R19 (.D(Input), .en(En19), .Q(OutR19), .clk(Clock), .clr(Clr19));
  Register #(.width(32)) R27 (.D(Input), .en(En27), .Q(OutR27), .clk(Clock), .clr(Clr27));
  Register #(.width(32)) R4 (.D(Input), .en(En4), .Q(OutR4), .clk(Clock), .clr(Clr4));
  Register #(.width(32)) R12 (.D(Input), .en(En12), .Q(OutR12), .clk(Clock), .clr(Clr12));
  Register #(.width(32)) R20 (.D(Input), .en(En20), .Q(OutR20), .clk(Clock), .clr(Clr20));
  Register #(.width(32)) R28 (.D(Input), .en(En28), .Q(OutR28), .clk(Clock), .clr(Clr28));
  Register #(.width(32)) R5 (.D(Input), .en(En5), .Q(OutR5), .clk(Clock), .clr(Clr5));
  Register #(.width(32)) R13 (.D(Input), .en(En13), .Q(OutR13), .clk(Clock), .clr(Clr13));
  Register #(.width(32)) R21 (.D(Input), .en(En21), .Q(OutR21), .clk(Clock), .clr(Clr21));
  Register #(.width(32)) R29 (.D(Input), .en(En29), .Q(OutR29), .clk(Clock), .clr(Clr29));
  Register #(.width(32)) R6 (.D(Input), .en(En6), .Q(OutR6), .clk(Clock), .clr(Clr6));
  Register #(.width(32)) R14 (.D(Input), .en(En14), .Q(Out14), .clk(Clock), .clr(Clr14));
  Register #(.width(32)) R22 (.D(Input), .en(En22), .Q(OutR22), .clk(Clock), .clr(Clr22));
  Register #(.width(32)) R30 (.D(Input), .en(En30), .Q(OutR30), .clk(Clock), .clr(Clr30));
  Register #(.width(32)) R7 (.D(Input), .en(En7), .Q(OutR7), .clk(Clock), .clr(Clr7));
  Register #(.width(32)) R15 (.D(Input), .en(En15), .Q(OutR15), .clk(Clock), .clr(Clr15));
  Register #(.width(32)) R23 (.D(Input), .en(En23), .Q(OutR23), .clk(Clock), .clr(Clr23));
  Register #(.width(32)) R31 (.D(Input), .en(En31), .Q(OutR31), .clk(Clock), .clr(Clr31));
endmodule
